// Logisim project trab.circ as structural Verilog: 1 circuit, main circuit main
module main (
  input  _1,
  input  [7:0] in_2,
  input  plus_1,
  input  Reset,
  input  Leitura_0__Escrita_1,
  output EOF,
  output [5:0] Braille_Dots,
  output [5:0] out_8
);

  wire clock_1_out, not_1_out, not_2_out, not_3_out;
  wire [1:0] bitselector_1_out, bitselector_2_out, bitselector_3_out;
  wire [7:0] counter_1_q;

  Clock clock_1 (.out(clock_1_out));
  Counter #(.ongoal("stay")) counter_1 (
    .load(_1), .D(in_2), .count(plus_1), .Q(counter_1_q), .carry(EOF), .clk(clock_1_out), .clr(Reset));
  assign out_8 = Leitura_0__Escrita_1 ? Braille_Dots : 6'bz;  // Controlled_Buffer controlled_buffer_1
  not not_1 (not_1_out, EOF);
  not not_2 (not_2_out, EOF);
  not not_3 (not_3_out, Leitura_0__Escrita_1);
  ROM #(.dataWidth(6)) rom_1 (.addr(counter_1_q), .data(Braille_Dots), .sel(not_1_out));
  RAM #(.dataWidth(6)) ram_1 (
    .addr(counter_1_q), .data(out_8), .sel(not_2_out), .clk(clock_1_out), .ld(not_3_out), .clr(Reset));
  BitSelector #(.width(6), .group(2)) bitselector_1 (.in(Braille_Dots), .out(bitselector_1_out), .sel(2'b10));
  DotMatrix #(.inputtype("row"), .matrixcols(2), .matrixrows(3), .dotshape("circle")) dotmatrix_1 (
    .row0(bitselector_1_out), .row1(bitselector_2_out), .row2(bitselector_3_out));
  BitSelector #(.width(6), .group(2)) bitselector_2 (.in(Braille_Dots), .out(bitselector_2_out), .sel(2'b01));
  BitSelector #(.width(6), .group(2)) bitselector_3 (.in(Braille_Dots), .out(bitselector_3_out), .sel(2'b00));

  // Notes on the sheet:
  //   ROM
  //   RAM
  //   contents of rom_1 (hex, n*v repeats v):
  //   20 28 30 34 2c 38 3c 2c 18 1c 26 22 32 36 26 3a 3e 2e 1a 1e 23 2b 1d 33 37 27
endmodule
